// Logisim project MIPSProcessor.circ as structural Verilog
module MIPS32 (
);

  // MIPSProgramROM mipsprogramrom_1: pin names not known
  // Incrementer incrementer_1: pin names not known
  // Mips_ALU mips_alu_1: pin names not known
  // RegisterFile registerfile_1: pin names not known
endmodule

module instructionFetch (
  input  Stall,
  output [31:0] inst,
  output [31:0] PCPlus4
);

  wire clock_1_out;
  wire [31:2] register_1_q;

  Register #(.width(32)) register_1 (
    .D(PCPlus4), .en(Stall), .clk(clock_1_out), .Q({register_1_q, PCPlus4[1:0]}));  // open: clr
  Clock clock_1 (.out(clock_1_out));
  // Incrementer #(.width(30)) incrementer_1: pin names not known; wires that end beside it: Stall, register_1_q, PCPlus4[31:2]
  // MIPSProgramROM mipsprogramrom_1: pin names not known; wires that end beside it: {register_1_q, PCPlus4[1:0]}, inst
endmodule

module instructionDecode (
  input  [31:0] inst,
  input  [31:0] PCPlus4,
  output [31:0] A,
  output [31:0] B,
  output [31:0] imm,
  output [4:0] Sa,
  output [3:0] ctrl,
  output [31:0] PCPlus4out
);


  assign PCPlus4out = PCPlus4;
endmodule

module shift (
  input  [3:0] func0to3,
  input  [4:0] Sa,
  input  [31:0] rsValue,
  output [3:0] ctrl,
  output [4:0] Saout
);

  wire [3:0] shiftsa_1_ctrl, shiftvariable_1_ctrl;
  wire [4:0] shiftsa_1_saout, shiftvariable_1_saout;

  shiftSa shiftsa_1 (.func0to3(func0to3), .Sa(Sa), .ctrl(shiftsa_1_ctrl), .Saout(shiftsa_1_saout));
  shiftVariable shiftvariable_1 (
    .funct0to3(func0to3), .rsValue(rsValue), .ctrl(shiftvariable_1_ctrl), .Saout(shiftvariable_1_saout));
  Multiplexer #(.width(4), .enable("false")) multiplexer_1 (
    .in0(shiftsa_1_ctrl), .in1(shiftvariable_1_ctrl), .out(ctrl), .sel(func0to3[2]));
  Multiplexer #(.width(5), .enable("false")) multiplexer_2 (
    .in0(shiftsa_1_saout), .in1(shiftvariable_1_saout), .out(Saout), .sel(func0to3[2]));
endmodule

module shiftVariable (
  input  [3:0] funct0to3,
  input  [31:0] rsValue,
  output [3:0] ctrl,
  output [4:0] Saout
);


  assign ctrl = {funct0to3[3], funct0to3[1], funct0to3[3], funct0to3[0]};
  assign Saout = rsValue[4:0];
endmodule

module shiftSa (
  input  [3:0] func0to3,
  input  [4:0] Sa,
  output [3:0] ctrl,
  output [4:0] Saout
);


  assign ctrl = {func0to3[3], func0to3[1], func0to3[2], func0to3[0]};
  assign Saout = Sa;
endmodule
